# Fritzing sketch 3-sensorToWebserver (saved by Fritzing 0.9.3b)
breadboards: 1

parts:
  Part1 = Arduino Uno (Rev3)
  DHT1 = DHT11 Humitidy and Temperature Sensor
  R1 = Photocell (LDR) [package=THT]
  R2 = Resistor [tolerance=±5% resistance=220 package="0805 [SMD]"]
  hc-sr1 = hc-sr04  # not connected

nets:
  N1: Part1.A0, R1.pin_1, R2.Pin_0
  N2: Part1.GND, R2.Pin_1
  N3: Part1.D2, DHT1.DATA
  5V: Part1.5V, DHT1.VDD, R1.pin_0

notes:
  DHT11 Sensor
  LDR Sensor
  A0
  Ultrasonic Sensor

custom parts:
  DHT11 Humitidy and Temperature Sensor: DHT11 Humidity and Temperature Sensor
